// Digital circuit BaseCircuits.dig as structural Verilog
module BaseCircuits (
);

  wire Clk_2_b, Clk_b, I_b, R_b, relaydt_1_p1, relaydt_1_p4, relaydt_2_p3, relaydt_3_p4, relaydt_3_p5,
       relaydt_5_p4, relaydt_6_p2, relaydt_7_p1, relaydt_9_p1, relaydt_9_p4, S_b;

  Switch S (.A(1'b1), .B(S_b));
  Switch R (.A(1'b1), .B(R_b));
  Switch Clk (.A(1'b1), .B(Clk_b));
  // RelayDT relaydt_1: pin names not known; wires that end beside it: relaydt_1_p1, 1'b0, 1'b1, relaydt_1_p4
  // RelayDT relaydt_2: pin names not known; wires that end beside it: Clk_b, 1'b0, relaydt_2_p3, relaydt_1_p1, relaydt_1_p4
  // RelayDT relaydt_3: pin names not known; wires that end beside it: S_b, 1'b0, S_b, relaydt_3_p4, relaydt_3_p5
  // RelayDT relaydt_4: pin names not known; wires that end beside it: R_b, 1'b0, relaydt_3_p5, 1'b1, relaydt_3_p4
  LightBulb Q_plus (.A(relaydt_1_p4), .B(1'b0));
  LightBulb Q (.A(S_b), .B(1'b0));
  LightBulb nQ (.A(relaydt_3_p5), .B(1'b0));
  // RelayDT relaydt_5: pin names not known; wires that end beside it: relaydt_1_p4, 1'b0, Clk_b, relaydt_5_p4, 1'b1, 1'b1
  // RelayDT relaydt_6: pin names not known; wires that end beside it: 1'b0, relaydt_6_p2
  LightBulb nQ_plus (.A(relaydt_5_p4), .B(1'b0));
  Switch I (.A(1'b1), .B(I_b));
  Switch Clk_2 (.A(1'b1), .B(Clk_2_b));
  // RelayDT relaydt_7: pin names not known; wires that end beside it: relaydt_7_p1, 1'b0, 1'b1, relaydt_2_p3
  // RelayDT relaydt_8: pin names not known; wires that end beside it: relaydt_6_p2, 1'b0, relaydt_5_p4, relaydt_7_p1, relaydt_2_p3
  LightBulb Q_2 (.A(relaydt_2_p3), .B(1'b0));
  // RelayDT relaydt_9: pin names not known; wires that end beside it: relaydt_9_p1, 1'b0, 1'b1, relaydt_9_p4
  // RelayDT relaydt_10: pin names not known; wires that end beside it: Clk_2_b, 1'b0, I_b, relaydt_9_p1, relaydt_9_p4
  LightBulb Q_3 (.A(relaydt_9_p4), .B(1'b0));

  // Notes on the sheet:
  //   SR Latch
  //   Clocked Invert
  //   D Flip-Flop
  //   On +Clk Q+ inverts
  //   On -Clk Q- inverts
  //   ~Q+ is always inverse of Q+
  //   Works by latching the value of Q- into
  //   the first D F-F on +Clk and latching the
  //   value of Q+ into the second D FF on
  //   -Clk. The two relays in the middle
  //   invert Clk and Q from the first D F-F.
endmodule
