// Digital circuit Counter4.dig as structural Verilog
module Counter4 (
  input  Clk,
  output Out_0,
  output Out_1,
  output Out_2,
  output Out_3
);

  wire relaydt_1_p1, relaydt_1_p5, relaydt_2_p3, relaydt_2_p7, relaydt_3_p1, relaydt_3_p5, relaydt_4_p3,
       relaydt_4_p7, relaydt_5_p1, relaydt_5_p5, relaydt_6_p3, relaydt_6_p7, relaydt_7_p1, relaydt_7_p5,
       relaydt_8_p4, relaydt_8_p8;

  // RelayDT #(.poles(2)) relaydt_1: pin names not known; wires that end beside it: relaydt_1_p1, 1'b0, 1'b1, Out_0, relaydt_1_p5, 1'b1
  // RelayDT #(.poles(2)) relaydt_2: pin names not known; wires that end beside it: Clk, 1'b0, relaydt_2_p3, relaydt_1_p1, Out_0, relaydt_2_p3, relaydt_2_p7, relaydt_1_p5
  // RelayDT #(.poles(2)) relaydt_3: pin names not known; wires that end beside it: relaydt_3_p1, 1'b0, 1'b1, Out_1, relaydt_3_p5, 1'b1
  // RelayDT #(.poles(2)) relaydt_4: pin names not known; wires that end beside it: relaydt_1_p5, 1'b0, relaydt_4_p3, relaydt_3_p1, Out_1, relaydt_4_p3, relaydt_4_p7, relaydt_3_p5
  // RelayDT #(.poles(2)) relaydt_5: pin names not known; wires that end beside it: relaydt_5_p1, 1'b0, 1'b1, Out_2, relaydt_5_p5, 1'b1
  // RelayDT #(.poles(2)) relaydt_6: pin names not known; wires that end beside it: relaydt_3_p5, 1'b0, relaydt_6_p3, relaydt_5_p1, Out_2, relaydt_6_p3, relaydt_6_p7, relaydt_5_p5
  // RelayDT #(.poles(2)) relaydt_7: pin names not known; wires that end beside it: relaydt_7_p1, 1'b0, 1'b1, Out_3, relaydt_7_p5, 1'b1
  // RelayDT #(.poles(2)) relaydt_8: pin names not known; wires that end beside it: relaydt_7_p5, relaydt_5_p5, 1'b0, relaydt_8_p4, relaydt_7_p1, Out_3, relaydt_8_p4, relaydt_8_p8, relaydt_7_p5
  // RelayDT relaydt_9: pin names not known; wires that end beside it: relaydt_2_p3, relaydt_2_p7, 1'b1, 1'b0
  // RelayDT relaydt_10: pin names not known; wires that end beside it: relaydt_4_p3, relaydt_4_p7, 1'b1, 1'b0
  // RelayDT relaydt_11: pin names not known; wires that end beside it: relaydt_6_p3, relaydt_6_p7, 1'b1, 1'b0
  // RelayDT relaydt_12: pin names not known; wires that end beside it: relaydt_8_p4, relaydt_8_p8, 1'b1, 1'b0
endmodule
